# Fritzing sketch Fritzing Design - Visual Only (saved by Fritzing 0.9.0b)
breadboards: 3

parts:
  LED3 = 8x8 LED Matrix (red)
  LED5 = 8x8 LED Matrix (red)
  Part3 = Spark Core (v1.0)
  LED6 = 8x8 LED Matrix (green)
  Part5 = Spark Core (v1.0)
  BUTTON1 = Waterproof Pushbutton (blue)
  BUTTON2 = Waterproof Pushbutton (red)
  R12 = Resistor [tolerance=±5% resistance=10k package=THT]
  R13 = Resistor [tolerance=±5% resistance=10k package=THT]
  Part6 = Spark Core (v1.0)
  R15 = Resistor [tolerance=±5% resistance=220 package=THT]
  T2 = TMP36 Temperature Sensor [package="TO92 [THT]"]
  C2 = Ceramic Capacitor [capacitance=0.01µF package="0603 [SMD, multilayer]"]
  PIR1 = PIR sensor

nets:
  N1: LED3.+, LED5.+, Part3.3V3*, LED6.+
  N2: LED3.-, LED5.-, Part3.GND, LED6.-
  N3: LED3.D, LED5.D, Part3.D0, LED6.D
  N4: LED3.C, LED5.C, Part3.D1, LED6.C
  N5: Part5.GND, BUTTON1.no_name_yet#5, BUTTON2.no_name_yet#5, R12.Pin_1, R13.Pin_1
  N6: Part5.D2, BUTTON1.no_name_yet#1, R12.Pin_0
  N7: Part5.D3, BUTTON2.no_name_yet#1, R13.Pin_0
  N8: Part5.D5, BUTTON1.no_name_yet#4
  N9: Part5.D6, BUTTON2.no_name_yet#3, BUTTON2.no_name_yet#4
  N10: Part5.3V3*, BUTTON1.no_name_yet#2, BUTTON2.no_name_yet#2
  N11: Part6.A7, T2.Vout, C2.1
  GND: Part6.GND, T2.GND, C2.0, PIR1.GND
  N12: Part6.D4, R15.Pin_1
  N13: Part6.3V3*, T2.+Vs, PIR1.SIG
  N14: R15.Pin_0, PIR1.VDD

custom parts:
  8x8 LED Matrix (red): 8x8 LED Matrix with I2C control (red)
  8x8 LED Matrix (green): 8x8 LED Matrix with I2C control (green)
  Waterproof Pushbutton (blue): Waterproof Illuminated Pushbutton (blue)
  Waterproof Pushbutton (red): Waterproof Illuminated Pushbutton (red)
